// Logisim project 16BitCPU.circ as structural Verilog: 1 circuit, main circuit main
module main (
);

  wire A_IN, A_OUT, ALU_OUT, B_IN, B_OUT, CLK, counter_1_carry, decoder_1_out0, decoder_1_out1,
       decoder_1_out2, decoder_1_out3, decoder_1_out4, decoder_1_out5, decoder_1_out6, decoder_1_out7,
       PC_ENABLE, PC_IN, PC_OUT, PC_RESET, pull_resistor_1_node, pull_resistor_2_node, pull_resistor_10_node,
       pull_resistor_11_node, pull_resistor_12_node, pull_resistor_13_node, RAM_ENABLE, RAM_STORE, RST;
  wire [1:0] ALU_FLAGS_SOURCE;
  wire [3:0] ALU_NIBBLE_1, ALU_NIBBLE_2, ALU_NIBBLE_3, ALU_NIBBLE_4;
  wire [6:0] register_2_q_3, register_3_q;
  wire [7:0] counter_1_q, counter_2_q;
  wire [7:4] rom_2_data, rom_3_data, rom_4_data;
  wire [7:6] rom_1_data;
  wire [11:0] register_2_q;
  wire [12:0] register_2_q_2;
  wire [15:0] MAIN_BUS, ram_1_dout, register_1_q;

  Pull_Resistor pull_resistor_1 (.node(pull_resistor_1_node));
  Register #(.width(16)) register_1 (
    .D(MAIN_BUS), .en(pull_resistor_1_node), .Q(register_1_q), .clk(CLK), .clr(pull_resistor_2_node));
  Pull_Resistor pull_resistor_2 (.node(pull_resistor_2_node));
  RAM #(.addrWidth(16), .dataWidth(16)) ram_1 (
    .addr(register_1_q), .we(RAM_STORE), .oe(RAM_ENABLE), .clk(CLK), .dout(ram_1_dout));  // open: din
  assign MAIN_BUS = RAM_ENABLE ? ram_1_dout : 16'bz;  // Controlled_Buffer controlled_buffer_1
  LED led_1 (.in(MAIN_BUS[15]));
  LED led_2 (.in(MAIN_BUS[14]));
  LED led_3 (.in(MAIN_BUS[13]));
  LED led_4 (.in(MAIN_BUS[12]));
  LED led_5 (.in(MAIN_BUS[11]));
  LED led_6 (.in(MAIN_BUS[10]));
  Clock clock_1 (.out(CLK));
  LED led_7 (.in(MAIN_BUS[9]));
  LED led_8 (.in(MAIN_BUS[8]));
  LED led_9 (.in(MAIN_BUS[7]));
  LED led_10 (.in(MAIN_BUS[6]));
  LED led_11 (.in(MAIN_BUS[5]));
  LED led_12 (.in(MAIN_BUS[4]));
  LED led_13 (.in(MAIN_BUS[3]));
  LED led_14 (.in(MAIN_BUS[2]));
  Pull_Resistor pull_resistor_3 (.node(MAIN_BUS));
  LED led_15 (.in(MAIN_BUS[1]));
  LED led_16 (.in(MAIN_BUS[0]));
  Pull_Resistor pull_resistor_4 (.node(RAM_STORE));
  Pull_Resistor #(.pull(1)) pull_resistor_5 (.node(RAM_ENABLE));
  Pull_Resistor pull_resistor_6 (.node(PC_ENABLE));
  Pull_Resistor pull_resistor_7 (.node(PC_RESET));
  Pull_Resistor pull_resistor_8 (.node(PC_IN));
  Pull_Resistor pull_resistor_9 (.node(PC_OUT));
  Pull_Resistor pull_resistor_10 (.node(pull_resistor_10_node));
  Counter counter_1 (
    .load(PC_IN), .D(MAIN_BUS[7:0]), .count(PC_ENABLE), .Q(counter_1_q), .carry(counter_1_carry), .up(1'b1),
    .clk(CLK), .clr(PC_RESET));
  assign MAIN_BUS[7:0] = PC_OUT ? counter_1_q : 8'bz;  // Controlled_Buffer controlled_buffer_2
  assign MAIN_BUS[15:8] = PC_OUT ? counter_2_q : 8'bz;  // Controlled_Buffer controlled_buffer_3
  Pull_Resistor pull_resistor_11 (.node(pull_resistor_11_node));
  Pull_Resistor pull_resistor_12 (.node(pull_resistor_12_node));
  Counter counter_2 (
    .load(PC_IN), .D(MAIN_BUS[15:8]), .count(counter_1_carry), .Q(counter_2_q), .up(1'b1), .clk(CLK),
    .clr(PC_RESET));  // open: carry
  ROM #(.addrWidth(13)) rom_1 (
    .addr({register_2_q_2[12:8], 3'b001, register_2_q_2[4:0]}),
    .data({rom_1_data, ALU_FLAGS_SOURCE, ALU_NIBBLE_4}));
  Pull_Resistor pull_resistor_13 (.node(pull_resistor_13_node));
  DipSwitch #(.number(24)) dipswitch_1 (
    .sw20(A_IN), .sw21(A_OUT), .sw22(B_IN), .sw23(B_OUT), .sw24(ALU_OUT));  // open: sw1, sw2, sw3, sw4, sw5, sw6, sw7, sw8, sw9, sw10, sw11, sw12, sw13, sw14, sw15, sw16, sw17, sw18, sw19
  assign MAIN_BUS = ALU_OUT ? {ALU_NIBBLE_4, ALU_NIBBLE_3, ALU_NIBBLE_2, ALU_NIBBLE_1} : 16'bz;  // Controlled_Buffer controlled_buffer_4
  Decoder #(.enable("false"), .select(3)) decoder_1 (
    .out0(decoder_1_out0), .out1(decoder_1_out1), .out2(decoder_1_out2), .out3(decoder_1_out3),
    .out4(decoder_1_out4), .out5(decoder_1_out5), .out6(decoder_1_out6), .out7(decoder_1_out7), .sel(3'b001));
  ROM #(.addrWidth(13)) rom_2 (
    .addr({register_2_q_2[8], register_2_q[11:8], 3'b001, register_2_q_2[0], register_2_q[3:0]}),
    .data({rom_2_data, ALU_NIBBLE_3}));
  Register #(.width(16)) register_2 (
    .D(MAIN_BUS), .en(A_IN), .clk(CLK), .Q({register_2_q_2[4:0], register_2_q[3:0], register_2_q_3}),
    .clr(RST));
  LED led_17 (.in(decoder_1_out0));
  LED led_18 (.in(decoder_1_out1));
  LED led_19 (.in(decoder_1_out2));
  LED led_20 (.in(decoder_1_out3));
  LED led_21 (.in(decoder_1_out4));
  LED led_22 (.in(decoder_1_out5));
  LED led_23 (.in(decoder_1_out6));
  LED led_24 (.in(decoder_1_out7));
  Register #(.width(16)) register_3 (
    .D(MAIN_BUS), .en(B_IN), .clk(CLK), .Q({register_2_q_2[12:8], register_2_q[11:8], register_3_q}),
    .clr(RST));
  assign MAIN_BUS = A_OUT ? {register_2_q_2[4:0], register_2_q[3:0], register_2_q_3} : 16'bz;  // Controlled_Buffer controlled_buffer_5
  assign MAIN_BUS = B_OUT ? {register_2_q_2[12:8], register_2_q[11:8], register_3_q} : 16'bz;  // Controlled_Buffer controlled_buffer_6
  ROM #(.addrWidth(13)) rom_3 (
    .addr({register_2_q[8], register_3_q[6:3], 3'b001, register_2_q[0], register_2_q_3[6:3]}),
    .data({rom_3_data, ALU_NIBBLE_2}));
  Pull_Resistor pull_resistor_14 (.node(RST));
  ROM #(.addrWidth(13)) rom_4 (
    .addr({register_3_q[3:0], 4'b0001, register_2_q_3[3:0], 1'b0}), .data({rom_4_data, ALU_NIBBLE_1}));

  // Notes on the sheet:
  //   Program Counter - 16Bit
  //   Register A - 16Bit
  //   DIV
  //   Register B - 16Bit
  //   ADD
  //   SUB
  //   AND
  //   OR
  //   XOR
  //   SHL
  //   MUL
endmodule
